# Fritzing sketch clock (saved by Fritzing 0.9.3b)

parts:
  J2 = Generic female header - 8 pins [form="♀ (female)" package=THT]
  J3 = Generic female header - 6 pins [form="♀ (female)" package=THT]
  J4 = Generic female header - 4 pins [form="♀ (female)" package=THT]

nets:
  N1: J2.pin3, J4.pin2
  N2: J2.pin4, J4.pin1
  N3: J2.pin7, J3.pin4
  N4: J2.pin8, J3.pin3

notes:
  1. Make connections
  2. Connect power (VCC and 5V) and ground (GND) . It is not on the diagram to make it clearer.
  3. Install "RTClib" by Adafruit
  4. Go to Clock example https://www.makerguides.com/tm1637-arduino-tutorial/
  5. Make new file copy the code in to it.
  6. Load and run.

custom parts:
  Generic female header - 8 pins: Generic female header
  Generic female header - 6 pins: Generic female header
  Generic female header - 4 pins: Generic female header
